# Fritzing sketch blink.shematik (saved by Fritzing 0.9.4)
breadboards: 1

parts:
  R1 = Resistor [tolerance=±5% resistance=220 package=THT]
  LED1 = smd LED [color="Red (633nm)" package="0805 [SMD]"]
  Part1 = Arduino Uno (Rev3)

nets:
  N1: R1.Pin_0, Part1.GND
  N2: R1.Pin_1, LED1.cathode
  N3: LED1.anode, Part1.D13/SCK
